# Fritzing sketch ThirdAssignment_LisaCocchia_793569 (saved by Fritzing 0.9.3b)
breadboards: 3

parts:
  U1 = NodeMCU V1.0
  DHT22 = AM2302 DHT22 Humidity and Temperature Sensor
  Solid_state_relay = Solid State High Level Relay Module [package=relay]
  WATER_PUMP = water pump/motor
  SERVO1 = Tower Pro SG90 servo [part_number=101246]
  Componente1 = Soil Moisture Sensor
  AHT22 = Adafruit AHT20 Temperature and Humidity Sensor [part_number="Adafruit #4566"]
  LED4 = smd LED [color="Yellow (592nm)" package="0805 [SMD]"]
  Piezo4 = Piezo Speaker - PC Mount [part_number=COM-07950]
  R16 = Resistor [tolerance=±5% resistance=200 package="0603 [SMD]"]
  R17 = Resistor [tolerance=±5% resistance=200 package="0603 [SMD]"]
  I2C_LCD_Display_(16x2)_3 = LCD1602-I2C
  U4 = NodeMCU V1.0
  PIR_-_SR602 = HC-SR501 Body Sensor Module
  R18 = Resistor [tolerance=±5% resistance=200 package="0603 [SMD]"]
  LED5 = smd LED [color="Yellow (592nm)" package="0805 [SMD]"]
  Part3 = MQ-4
  LED6 = smd LED [color="Yellow (592nm)" package="0805 [SMD]"]
  LED7 = smd LED [color="Yellow (592nm)" package="0805 [SMD]"]
  R19 = Resistor [tolerance=±1% resistance=3.3k package="0603 [SMD]"]
  R20 = Resistor [tolerance=±1% resistance=2.2k power=1.7kW part_number=1.7kΩ package="0603 [SMD]"]
  R22 = Resistor [tolerance=±5% resistance=200 package="0603 [SMD]"]
  R23 = Resistor [tolerance=±5% resistance=200 package="0603 [SMD]"]
  U5 = NodeMCU V1.0
  SERVO2 = Tower Pro SG90 servo [part_number=101246]

nets:
  N1: U1.D5, Solid_state_relay.CH1
  N2: U1.D6, DHT22.DAT
  N3: U1.D7, SERVO1.Signal
  N4: U1.A0, Componente1.SIG
  VCC: DHT22.VCC, Componente1.VCC
  GND: DHT22.GND, Componente1.GND
  N5: Solid_state_relay.DC+, Solid_state_relay.B1, SERVO1.+5V
  N6: Solid_state_relay.A1, WATER_PUMP.pin_2
  N7: Solid_state_relay.DC-, WATER_PUMP.pin_1, SERVO1.GND
  VCC_2: AHT22.VCC, U4.3V3
  GND_2: AHT22.GND, LED4.cathode, Piezo4.GND, I2C_LCD_Display_(16x2)_3.GND, U4.GND, PIR_-_SR602.GND, LED5.cathode
  N8: AHT22.SCL, I2C_LCD_Display_(16x2)_3.SCL, U4.D1
  N9: AHT22.SDA, I2C_LCD_Display_(16x2)_3.SDA, U4.D2
  N10: LED4.anode, R17.Pin_0
  N11: Piezo4.VCC, R16.Pin_0
  N12: R16.Pin_1, U4.D6
  N13: R17.Pin_1, U4.D3
  VCC_3: I2C_LCD_Display_(16x2)_3.VCC, U4.Vin, PIR_-_SR602.VCC
  N14: U4.D4, R18.Pin_1
  N15: U4.D7, PIR_-_SR602.OUT
  N16: R18.Pin_0, LED5.anode
  VCC_4: Part3.VCC, U5.Vin, SERVO2.+5V
  GND_3: Part3.GND, LED6.cathode, LED7.cathode, R19.Pin_1, U5.GND, SERVO2.GND
  N17: Part3.AO, R20.Pin_0
  N18: LED6.anode, R23.Pin_0
  N19: LED7.anode, R22.Pin_0
  N20: R19.Pin_0, R20.Pin_1, U5.A0
  N21: R22.Pin_1, U5.D3
  N22: R23.Pin_1, U5.D4
  N23: U5.D5, SERVO2.Signal

custom parts:
  NodeMCU V1.0: ESP8266 based NodeMCU
  Solid State High Level Relay Module: 5V Omron solid state relay 240V 2A output with resistance fuse.
  water pump/motor: WATER PUMP BY ARDUBLOCKTR
  Tower Pro SG90 servo: Original file by John De Cristofaro http://www.adafruit.com/products/1449 Adafruit Feedback Servo (Small) Edited by: e-radionica.com 28/9/2015
  Adafruit AHT20 Temperature and Humidity Sensor: The AHT20 is a nice but inexpensive temperature and humidity sensor from the same folks that brought us the DHT22. You can take sensor readings as often as you like, and it uses standard I2C so its super easy to use with any Arduino or Linux/Raspberry Pi board. This sensor has a typical accuracy of +- 2% relative humidity, and +-0.3 °C. There is only one I2C address so its not a good option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
  Piezo Speaker - PC Mount: This is a small 12mm round speaker that operates around the audible 2kHz range. You can use these speakers to create simple music or user interfaces. Each speaker is PTH solderable and requires an operating voltage of 3.5-5V with a mean current of 35mA max. These speakers also have a typical sound output of 95 dBA and a coil resistance of 42 ±6.3 ohms.
  LCD1602-I2C: A standard character display, usually with 2x16 characters. Comes in many colors with LCM1602 IIC attached.
  HC-SR501 Body Sensor Module: Pyroelectric Infrared PIR Motion Sensor Detector Module
